# Fritzing sketch modelo_fritzing (saved by Fritzing 0.9.9b)
circuit board: 19.4742cm x 10.077cm

parts:
  J1 = Basic Servo
  SPKR1 = Loudspeaker
  Mod1 = Raspberry Pi 4B

nets:
  GND: J1.gnd, SPKR1.pin2, Mod1.GND
  VCC: J1.vcc, Mod1.5V
  N1: J1.pulse, Mod1.GPIO14
  N2: SPKR1.pin1, Mod1.GPIO18
